// Logisim project Additional Ciruit.circ as structural Verilog: 1 circuit, main circuit main
module main (
  input  [6:0] In_A,
  input  [6:0] In_B,
  input  [6:0] In_C,
  input  [6:0] In_D,
  input  [2:0] No_of_Patterns,
  input  ON_OF_Switch,
  input  [6:0] no__of_pieces,
  input  Count_Enable,
  output Y
);

  wire and_1_out, and_2_out, comparator_1_gt, comparator_2_eq, Frequency_adjusted_CLK_out, multiplexer_2_out,
       nor_1_out, not_1_out, not_2_out, or_1_out, or_2_out, or_3_out, RESET_Button_out;
  wire [1:0] counter_2_q;
  wire [6:0] counter_1_q, counter_3_q, multiplexer_1_out, multiplier_1_out, subtractor_1_out;

  or or_1 (or_1_out, RESET_Button_out, not_1_out);
  Multiplier #(.width(7)) multiplier_1 (
    .a(no__of_pieces), .b({4'b0000, No_of_Patterns}), .out(multiplier_1_out));  // open: cin, cout
  Counter #(.width(7), .max('h7f)) counter_1 (
    .count(and_1_out), .Q(counter_1_q), .clk(nor_1_out), .clr(or_1_out));  // open: load, D, carry
  not not_1 (not_1_out, Count_Enable);
  Button RESET_Button (.out(RESET_Button_out));
  Comparator #(.width(7)) comparator_1 (.a(counter_1_q), .b(multiplier_1_out), .gt(comparator_1_gt));  // open: eq, lt
  not not_2 (not_2_out, comparator_1_gt);
  and and_1 (and_1_out, not_2_out, ON_OF_Switch);
  Counter #(.width(2), .max('h3)) counter_2 (
    .count(and_1_out), .Q(counter_2_q), .clk(nor_1_out), .clr(or_2_out));  // open: load, D, carry
  or or_2 (or_2_out, RESET_Button_out, multiplexer_2_out);
  Multiplexer #(.select(2), .width(7)) multiplexer_1 (
    .in0(In_A), .in1(In_B), .in2(In_C), .in3(In_D), .out(multiplexer_1_out), .sel(counter_2_q));  // open: en
  and and_2 (and_2_out, counter_2_q[1], counter_2_q[0]);
  Multiplexer #(.select(2)) multiplexer_2 (
    .in0(1'b1), .in1(counter_2_q[1]), .in2(and_2_out), .in3(1'b0), .out(multiplexer_2_out),
    .sel(subtractor_1_out[1:0]));  // open: en
  Subtractor #(.width(7)) subtractor_1 (
    .a({4'b0000, No_of_Patterns}), .b(7'b0000001), .out(subtractor_1_out));  // open: bin, bout
  Comparator #(.width(7)) comparator_2 (.a(counter_3_q), .b(multiplexer_1_out), .eq(comparator_2_eq));  // open: gt, lt
  nor nor_1 (nor_1_out, counter_3_q[0], counter_3_q[1], counter_3_q[2], counter_3_q[3], counter_3_q[4], counter_3_q[5], counter_3_q[6]);
  Counter #(.width(7), .max('h7f)) counter_3 (
    .count(and_1_out), .Q(counter_3_q), .clk(Frequency_adjusted_CLK_out), .clr(or_3_out));  // open: load, D, carry
  or or_3 (or_3_out, comparator_2_eq, RESET_Button_out);
  and and_3 (Y, and_1_out, Frequency_adjusted_CLK_out, nor_1_out);
  Clock Frequency_adjusted_CLK (.out(Frequency_adjusted_CLK_out));

  // Notes on the sheet:
  //   PROJECT 30 - THE GARMENT FACTORY
endmodule
