// Logisim project Main Circuit.circ as structural Verilog: 1 circuit, main circuit main
module main (
  input  [3:0] A,
  input  [3:0] B,
  input  [3:0] C,
  input  [1:0] No_of_Pattern,
  input  On_Off_Switch,
  output Y
);

  wire and_1_out, clock_1_out, comparator_1_eq, multiplexer_2_out, nor_1_out, not_1_out, or_1_out, or_2_out;
  wire [1:0] counter_1_q;
  wire [3:0] counter_2_q, multiplexer_1_out;

  or or_1 (or_1_out, not_1_out, multiplexer_2_out);
  not not_1 (not_1_out, On_Off_Switch);
  Counter #(.width(2), .max('h3)) counter_1 (
    .count(On_Off_Switch), .Q(counter_1_q), .clk(nor_1_out), .clr(or_1_out));  // open: load, D, carry
  and and_1 (and_1_out, counter_1_q[1], counter_1_q[0]);
  Multiplexer #(.select(2), .width(4)) multiplexer_1 (
    .in0(A), .in1(B), .in2(C), .in3(4'b0000), .out(multiplexer_1_out), .sel(counter_1_q));  // open: en
  Multiplexer #(.select(2)) multiplexer_2 (
    .in0(1'b1), .in1(1'b1), .in2(counter_1_q[1]), .in3(and_1_out), .out(multiplexer_2_out),
    .sel(No_of_Pattern));  // open: en
  Clock clock_1 (.out(clock_1_out));
  Comparator #(.width(4)) comparator_1 (.a(counter_2_q), .b(multiplexer_1_out), .eq(comparator_1_eq));  // open: gt, lt
  nor nor_1 (nor_1_out, counter_2_q[0], counter_2_q[1], counter_2_q[2], counter_2_q[3]);
  Counter #(.width(4), .max('hf)) counter_2 (
    .count(On_Off_Switch), .Q(counter_2_q), .clk(clock_1_out), .clr(or_2_out));  // open: load, D, carry
  or or_2 (or_2_out, not_1_out, comparator_1_eq);
  and and_2 (Y, On_Off_Switch, clock_1_out, nor_1_out);

  // Notes on the sheet:
  //   OR
  //   Gate
  //   NOT Gate
  //   2-BIT COUNTER
  //   AND GATE
  //   PROJECT 30 - THE GARMENT FACTORY
  //   4-BIT COMPARATOR
  //   Frequency Adjusted
  //   CLK
  //   4 to 1 NOR Gate
  //   4-BIT COUNTER
  //   OR Gate
  //   3 to 1 AND Gate
endmodule
